// Logisim project 13.circ as structural Verilog: 1 circuit, main circuit main
module main (
  input  in_1,
  input  in_2,
  input  in_3,
  input  [2:0] in_4,
  output out_5,
  output out_6,
  output out_7,
  output out_8,
  output out_9,
  output out_10,
  output out_11,
  output out_12,
  output out_13,
  output out_14,
  output out_15,
  output out_16,
  output out_17,
  output out_18,
  output out_19,
  output out_20
);

  wire not_1_out, not_2_out, not_3_out;

  not not_1 (not_1_out, in_1);
  not not_2 (not_2_out, in_2);
  not not_3 (not_3_out, in_3);
  and and_1 (out_11, not_1_out, not_2_out, not_3_out);
  and and_2 (out_14, not_1_out, not_2_out, in_3);
  and and_3 (out_15, not_1_out, in_2, not_3_out);
  and and_4 (out_16, not_1_out, in_2, in_3);
  and and_5 (out_17, in_1, not_2_out, not_3_out);
  and and_6 (out_18, in_1, not_2_out, not_3_out);
  and and_7 (out_19, in_1, in_2, not_3_out);
  and and_8 (out_20, in_1, in_2, in_3);
  Decoder #(.select(3)) decoder_1 (
    .out0(out_5), .out1(out_6), .out2(out_7), .out3(out_8), .out4(out_9), .out5(out_10), .out6(out_12),
    .out7(out_13), .sel(in_4));  // open: en
endmodule
